# Fritzing sketch legendary-dashboard-ESP32 (saved by Fritzing 0.9.4)

parts:
  Part1 = BME280 Breakout
  Part2 = Waveshare 4.2" 400×300 ePaper Display Module
  Mod1 = TTGO-T-Call-V1.3-ESP32 [package=THT]

nets:
  N1: Part1.VCC, Mod1.25
  GND: Part1.GND, Part2.GND, Mod1.GND
  N2: Part1.SCL, Mod1.32
  N3: Part1.SDA, Mod1.33
  VCC: Part2.VCC, Mod1.3V3
  N4: Part2.DIN, Mod1.15
  N5: Part2.CLK, Mod1.14
  N6: Part2.CS, Mod1.19
  N7: Part2.DC, Mod1.18
  N8: Part2.RST, Mod1.0
  N9: Part2.BUSY, Mod1.2

custom parts:
  BME280 Breakout: SparkFun Atmospheric Sensor Breakout - BME280 SEN-13676 The SparkFun BME280 Atmospheric Sensor Breakout is the easy way to measure barometric pressure, humidity, and temperature readings all without taking up too much space. Basically, anything you need to know about atmospheric conditions you can find out from this tiny breakout. The BME280 Breakout has been design to be used in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
  TTGO-T-Call-V1.3-ESP32: LILYGO® TTGO T-Call V1.3 ESP32 Wireless Module GPRS Antenna SIM Card SIM800L Module
